# Fritzing sketch schematics (saved by Fritzing 0.9.3b)
breadboards: 1

parts:
  WeMos_D1_Mini1 = WeMos D1 Mini
  HC-SR04_Sensor_1 = HC-SR04 Ultrasonic Distance Sensor
  R1 = Resistor [tolerance=±5% resistance=1k package="0805 [SMD]"]
  R2 = Resistor [tolerance=±5% resistance=2.2k package="0805 [SMD]"]

nets:
  5V: WeMos_D1_Mini1.5V, HC-SR04_Sensor_1.VCC
  N1: WeMos_D1_Mini1.D6, R1.Pin_1, R2.Pin_1
  N2: WeMos_D1_Mini1.D7, HC-SR04_Sensor_1.TRIG
  GND: WeMos_D1_Mini1.G, HC-SR04_Sensor_1.ECHO, R2.Pin_0
  N3: HC-SR04_Sensor_1.GND, R1.Pin_0
